# Fritzing sketch wiring (saved by Fritzing 0.9.2b)

parts:
  Part1 = Arduino Ethernet Shield (Rev3)
  R1 = Resistor [tolerance=±5% resistance=10k package=THT]
  DHT11 = DHT11 Humitidy and Temperature Sensor
  S1 = SWITCH-MOMENTARY-2 [package=tactile-switch-1101ne]
  S2 = SWITCH-MOMENTARY-2 [package=tactile-switch-1101ne]
  R2 = Resistor [tolerance=±5% resistance=10k package=THT]
  D1 = Diode [package=diode-1n4001]
  J1 = Screw terminal - 2 pins [package=THT]
  J2 = Screw terminal - 2 pins [package=THT]
  Q1 = Basic FET N-Channel [package="TO220 [THT]"]

nets:
  N1: Part1.5V, S1.2, S2.2
  N2: Part1.GND, R2.Pin_1, J1.pin2, Q1.source
  N3: Part1.D2, R1.Pin_0, DHT11.DATA
  N4: Part1.PWM_D3, S1.1, S2.1, R2.Pin_0, Q1.gate
  N5: Part1.VIN, D1.C, J2.pin1
  N6: R1.Pin_1, DHT11.VDD
  N7: D1.A, J1.pin1
  N8: J2.pin2, Q1.drain

notes:
  <-- + 12V input DC
  <-- GND input
  GND output -->
  + 12V LEDs output -->
  + 12V input DC -->
  GND input -->
  <-- GND output
  <-- + 12V LEDs output
  G
  D
  S

custom parts:
  DHT11 Humitidy and Temperature Sensor: DHT11 Humidity and Temperature Sensor
